# Fritzing sketch useless box prototyping (saved by Fritzing 0.9.3b)
breadboards: 2

parts:
  Part1 = Arduino Uno (Rev3)  # not connected
  R1 = Resistor [tolerance=±5% resistance=220 package="0402 [SMD]"]
  U1 = SWITCH_SPDT [package=kps-1290]
  R2 = Resistor [tolerance=±5% resistance=220 package="0402 [SMD]"]
  J1 = Basic Servo
  LED1 = smd LED [color="Red (633nm)" package="1206 [SMD]"]
  Part2 = Prototyping Shield
  R3 = Resistor [tolerance=±5% resistance=220 package="0402 [SMD]"]

nets:
  N1: R1.Pin_0, Part2.GND#100
  N2: R1.Pin_1, LED1.cathode
  N3: U1.O, R2.Pin_0, Part2.D11_PWM/MOSI
  N4: U1.P, Part2.5V#96
  N5: U1.S, Part2.D12/MISO, R3.Pin_0
  N6: R2.Pin_1, Part2.GND#98
  N7: J1.gnd, Part2.GND#101
  N8: J1.vcc, Part2.5V#95
  N9: J1.pulse, Part2.D10_PWM/SS
  N10: LED1.anode, Part2.5V#94
  N11: Part2.GND#97, R3.Pin_1

custom parts:
  Prototyping Shield: The Arduino Uno is a microcontroller board based on the ATmega328 (datasheet). It has 14 digital input/output pins (of which 6 can be used as PWM outputs), 6 analog inputs, a 16 MHz ceramic resonator, a USB connection, a power jack, an ICSP header, and a reset button. It contains everything needed to support the microcontroller; simply connect it to a computer with a USB cable or power it with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

// code stored in the sketch: Untitled2.ino

