# Fritzing sketch useless box (saved by Fritzing 0.9.3b)
breadboards: 2

parts:
  Part1 = Arduino Uno (Rev3)
  R1 = Resistor [tolerance=±5% resistance=220 package="0402 [SMD]"]
  U1 = SWITCH_SPDT [package=kps-1290]
  R2 = Resistor [tolerance=±5% resistance=220 package="0402 [SMD]"]

nets:
  N1: Part1.D10_PWM/SS, R1.Pin_0, U1.S
  N2: Part1.D11_PWM/MOSI, U1.O, R2.Pin_0
  N3: Part1.5V, U1.P
  N4: Part1.GND, R1.Pin_1, R2.Pin_1

// code stored in the sketch: Untitled2.ino
#include <Servo.h>
//Useless Box
//Johnny Krosby, Lucy Gray
//flip switch --> flip switch back

Servo myServo;

int origin = 0; //variable for when the servo is in its original position
int closing = 0; //variable for when the servo is touching switch
int delayVar = 0; //how long each delay lasts
int servoPin = 0;
int switchPinClose = 10; //if(HIGH){DUCK ATTACK;}
int switchPinOpen = 11; //if(HIGH){HUMAN ATTACK;}
int val1 = 0; //close
int val2 = 0; //open
int servoAngle = 0; //variable used for servo angle

void setup() {
  origin = 0;
  closing = 90;
  Serial.begin(9600);
  pinMode(servoPin, OUTPUT);
  pinMode(switchPinClose, INPUT);
  pinMode(switchPinOpen, INPUT);
  myServo.attach(servoPin);
  myServo.write(origin);
  delayVar = 0;
}

void loop() {

  val1 = digitalRead(switchPinClose);
  val2 = digitalRead(switchPinOpen);
  Serial.print(val1);
  Serial.println(" = val1");

  Serial.print("             ");
  Serial.print(val2);
  Serial.print(" = val2");
  Serial.print("         ");
  Serial.print(servoAngle);
  Serial.println(" = servoAngle");
//if the switch is pointing towards the duck then bring duck towards switch for DUCK ATTACK
  if (val1 == HIGH && val2 == LOW) {
    //switch toward box
    servoAngle = closing;
    myServo.writeMicroseconds(closing);
    delay(delayVar);
  }
//if the switch is pointing towards the human then bring duck back to original place
  else if (val1 == LOW && val2 == HIGH) {
    //switch towards human
    servoAngle = origin;
    myServo.writeMicroseconds(origin);
    delay(delayVar);
  }


}
//References

//https://www.arduino.cc/en/tutorial/pushbutton
//https://create.arduino.cc/projecthub/SBR/working-with-two-leds-and-two-push-buttons-1d4182       wiring
//https://create.arduino.cc/projecthub/glowascii/button-arduino-basics-5ecffc       more wiring
